# Fritzing sketch Diagrama (saved by Fritzing 0.8.3b)
breadboards: 1

parts:
  Part4 = Arduino Uno (Rev3)
  U9 = G3VM-61E1 [package=g3vm-61e1]
  L2 = Solenoid
  U10 = SLIDER [package=slider]
  U11 = SLIDER [package=slider]
  U12 = SLIDER [package=slider]

nets:
  N1: Part4.A0, U12.S
  N2: Part4.A1, U11.S
  N3: Part4.A2, U10.S
  N4: Part4.GND, U9.P$1, U10.A, U11.A, U12.A
  N5: Part4.D7, U9.P$3
  N6: Part4.5V, U9.P$2, U10.E, U11.E, U12.E
  N7: U9.P$6, L2.pin2

notes:
  Válvula Solenoide
  + Fuente de - alimentación (12 V)
