# Fritzing sketch Diagrama (saved by Fritzing 0.8.3b)
breadboards: 1

parts:
  Part1 = Arduino Uno (Rev3)
  Part3 = Real Time Clock Module - DS1307 RTC Breakout Board
  U8 = G3VM-61E1 [package=g3vm-61e1]
  V1 = AC Power [voltage=5 frequency=60]  # not connected
  L1 = Solenoid

nets:
  5V: Part1.5V, Part3.5V, U8.P$5
  GND: Part1.GND, Part3.GND, U8.P$4
  N1: Part1.A4/SDA, Part3.SDA
  N2: Part1.A5/SCL, Part3.SCL
  N3: Part1.D2, U8.P$6
  N4: U8.P$1, L1.pin2

notes:
  + Fuente de - alimentación (12 V)
  Válvula Solenoide
