# Fritzing sketch Diagrama_Alimentacion_Aislada (saved by Fritzing 0.9.3b)

parts:
  Part1 = Arduino Uno (Rev3)
  Part4 = Sunny Buddy MPPT LiPo Charger
  M1 = MT3608 Module
  Part5 = Solar Cell
  U1 = LIPO-2000mAh [package=lipo-2000]  # not connected

nets:
  N1: Part1.5V, M1.pin3
  N2: Part1.GND, M1.pin4
  N3: Part4.Secondary_+, Part5.+
  N4: Part4.Secondary_-, Part5.-
  N5: Part4.Load_+_(Screw_Terminal), M1.pin2
  N6: Part4.Load_-_(Screw_Terminal), M1.pin1

notes:
  Batería intercambiable por celdas de 3.7 V en paralelo

custom parts:
  Sunny Buddy MPPT LiPo Charger: Switch-mode MPPT charger for single cell LiPo batteries. Accepts up to 20V solar cell input.
  MT3608 Module: MT3608 Boost Converter Module Links: Aerosemi MT3608 2A Step Up Converter datasheet
