# Fritzing sketch Diagrama_Estacion (saved by Fritzing 0.9.3b)
breadboards: 1

parts:
  Part1 = Arduino Uno (Rev3)
  LCD1 = LCD screen
  LCM1602_IIC1 = LCM1602 IIC [part_number="LCM1602 IIC" chip_label="LCM1602 IIC" package="DIP (Dual Inline) [THT]"]
  AM1 = AM2302 Humidity and Temperature Sensor
  SD_card_module1 = SD Card Module
  J1 = RJ11 Jack [package=rj11-6]
  R1 = Resistor [tolerance=±1% resistance=1k package=THT]
  R2 = Resistor [tolerance=±5% resistance=1k package=THT]
  D6 = Rectifier Diode 10A [part_number=P1000K]
  D7 = Rectifier Diode 10A [part_number=P1000K]
  D8 = Rectifier Diode 10A [part_number=P1000K]
  D9 = Rectifier Diode 10A [part_number=P1000K]
  R3 = Resistor [tolerance=±5% resistance=1k package=THT]
  R4 = Resistor [tolerance=±5% resistance=1k package=THT]

nets:
  N1: Part1.A0, R1.Pin_0, D8.anode, D9.cathode
  N2: Part1.A4/SDA, LCM1602_IIC1.SDA
  N3: Part1.A5/SCL, LCM1602_IIC1.SCL
  N4: Part1.D9_PWM, AM1.DATA
  N5: Part1.D10_PWM/SS, SD_card_module1.CS
  N6: Part1.D11_PWM/MOSI, SD_card_module1.MOSI
  N7: Part1.D12/MISO, SD_card_module1.MISO
  N8: Part1.D13/SCK, SD_card_module1.SCK
  GND: Part1.GND, LCM1602_IIC1.GND, AM1.GND, SD_card_module1.GND, D7.anode, D9.anode, R3.Pin_0, R4.Pin_0
  N9: Part1.D3_PWM, R2.Pin_0, D6.anode, D7.cathode
  5V: Part1.5V, LCM1602_IIC1.VCC, AM1.VDD, SD_card_module1.+5, D6.cathode, D8.cathode
  VSS: LCD1.VSS, LCM1602_IIC1.VSS
  VDD: LCD1.VDD, LCM1602_IIC1.VDD
  N10: LCD1.V0, LCM1602_IIC1.V0
  N11: LCD1.RS, LCM1602_IIC1.RS
  N12: LCD1.R/W, LCM1602_IIC1.RW
  N13: LCD1.E, LCM1602_IIC1.E
  N14: LCD1.DB0, LCM1602_IIC1.D0
  N15: LCD1.DB1, LCM1602_IIC1.D1
  N16: LCD1.DB2, LCM1602_IIC1.D2
  N17: LCD1.DB3, LCM1602_IIC1.D3
  N18: LCD1.DB4, LCM1602_IIC1.D4
  N19: LCD1.DB5, LCM1602_IIC1.D5
  N20: LCD1.DB6, LCM1602_IIC1.D6
  N21: LCD1.DB7, LCM1602_IIC1.D7
  N22: LCD1.LED+, LCM1602_IIC1.A
  N23: LCD1.LED-, LCM1602_IIC1.K
  N24: LCM1602_IIC1.LED_A, LCM1602_IIC1.LED_B
  N25: J1.2, R1.Pin_1
  N26: J1.4, R3.Pin_1
  N27: J1.5, R4.Pin_1

notes:
  Conexión de los sensores de viento, equivalente al weather shield de sparkfun

custom parts:
  LCM1602 IIC: I2C-Module to use a 1602 or 2004 LCD on with the wire.h libory Serial LCD Modul
  SD Card Module: SD Card Module Slot Socket Reader For Arduino ARM MCU
