# Fritzing sketch Diagrama (saved by Fritzing 0.8.3b)
breadboards: 1

parts:
  Part1 = Arduino Uno (Rev3)
  S11 = Round Pushbutton
  S13 = Toggle Switch [package=THT]
  VCC2 = Battery block 9V
  R1 = Resistor [tolerance=±5% resistance=4.7k package="0805 [SMD]"]
  LCD2 = LCD screen
  LCM1602_IIC2 = LCM1602 IIC [part_number="LCM1602 IIC" chip_label="LCM1602 IIC" package="DIP (Dual Inline) [THT]"]
  SENS1 = SoilWatch 10

nets:
  N1: Part1.A0, SENS1.OUT
  N2: Part1.A4/SDA, LCM1602_IIC2.SDA
  N3: Part1.A5/SCL, LCM1602_IIC2.SCL
  GND: Part1.GND, VCC2.-, R1.Pin_0, LCM1602_IIC2.GND, SENS1.GND
  N4: Part1.D7, S11.leg1, R1.Pin_1
  VCC: Part1.5V, S11.leg0, LCM1602_IIC2.VCC, SENS1.VCC
  N5: Part1.VIN, S13.COM
  N6: S13.L1, VCC2.+
  VSS: LCD2.VSS, LCM1602_IIC2.VSS
  VDD: LCD2.VDD, LCM1602_IIC2.VDD
  N7: LCD2.V0, LCM1602_IIC2.V0
  N8: LCD2.RS, LCM1602_IIC2.RS
  N9: LCD2.R/W, LCM1602_IIC2.RW
  N10: LCD2.E, LCM1602_IIC2.E
  N11: LCD2.DB0, LCM1602_IIC2.D0
  N12: LCD2.DB1, LCM1602_IIC2.D1
  N13: LCD2.DB2, LCM1602_IIC2.D2
  N14: LCD2.DB3, LCM1602_IIC2.D3
  N15: LCD2.DB4, LCM1602_IIC2.D4
  N16: LCD2.DB5, LCM1602_IIC2.D5
  N17: LCD2.DB6, LCM1602_IIC2.D6
  N18: LCD2.DB7, LCM1602_IIC2.D7
  N19: LCD2.LED+, LCM1602_IIC2.A
  N20: LCD2.LED-, LCM1602_IIC2.K
  N21: LCM1602_IIC2.LED_A, LCM1602_IIC2.LED_B

custom parts:
  LCM1602 IIC: I2C-Module to use a 1602 or 2004 LCD on with the wire.h libory Serial LCD Modul
  SoilWatch 10: SoilWatch 10 - Capacitive soil moisture sensor
